# Fritzing sketch FINAL_10 (saved by Fritzing 0.9.3b)
breadboards: 3

parts:
  元件1 = node32s
  S1 = Pushbutton [package="[SMD]"]
  OLED_I2C2 = OLED 128x64 I2C Monochrome Display
  元件4 = Passive Buzzer
  DHT11_1 = DHT11 module
  J1 = Basic Servo
  7_Segment1 = 7 Segment Display
  7_Segment2 = 7 Segment Display
  7_Segment3 = 7 Segment Display
  7_Segment4 = 7 Segment Display
  元件5 = node32s
  M2 = DC Motor
  RY2 = KF-301 Relay [package=THT]
  VCC2 = Battery
  S3 = Pushbutton [package="[SMD]"]
  R1 = Resistor [tolerance=±5% resistance=330 package=THT]
  R2 = Resistor [tolerance=±5% resistance=330 package=THT]
  R3 = Resistor [tolerance=±5% resistance=330 package=THT]
  R4 = Resistor [tolerance=±5% resistance=330 package=THT]
  R5 = Resistor [tolerance=±5% resistance=330 package=THT]
  R6 = Resistor [tolerance=±5% resistance=330 package=THT]
  R7 = Resistor [tolerance=±5% resistance=330 package=THT]
  R8 = Resistor [tolerance=±5% resistance=330 package=THT]
  R9 = Resistor [tolerance=±5% resistance=330 package=THT]
  R10 = Resistor [tolerance=±5% resistance=330 package=THT]
  R11 = Resistor [tolerance=±5% resistance=330 package=THT]
  R12 = Resistor [tolerance=±5% resistance=330 package=THT]
  R13 = Resistor [tolerance=±5% resistance=330 package=THT]
  R14 = Resistor [tolerance=±5% resistance=330 package=THT]
  R15 = Resistor [tolerance=±5% resistance=330 package=THT]
  R16 = Resistor [tolerance=±5% resistance=330 package=THT]
  R17 = Resistor [tolerance=±5% resistance=330 package=THT]
  R18 = Resistor [tolerance=±5% resistance=330 package=THT]
  R19 = Resistor [tolerance=±5% resistance=330 package=THT]
  LED2 = LED - 5mm [color="Blue (505nm)" package="5 mm [THT]"]
  LED3 = LED - 5mm [color="White (4500K)" package="5 mm [THT]"]
  LED4 = LED - 5mm [color="Yellow (585nm)" package="5 mm [THT]"]
  LED5 = LED - 5mm [color="Red (635nm)" package="5 mm [THT]"]
  LED6 = LED - 5mm [color="White (4500K)" package="5 mm [THT]"]
  LED7 = LED - 5mm [color="Blue (505nm)" package="5 mm [THT]"]
  R21 = Resistor [tolerance=±5% resistance=330 package=THT]
  R22 = Resistor [tolerance=±5% resistance=330 package=THT]
  R23 = Resistor [tolerance=±5% resistance=330 package=THT]
  R24 = Resistor [tolerance=±5% resistance=330 package=THT]
  R25 = Resistor [tolerance=±5% resistance=330 package=THT]
  R26 = Resistor [tolerance=±5% resistance=330 package=THT]
  R27 = Resistor [tolerance=±5% resistance=330 package=THT]
  LED1 = LED - 5mm [color="Red (635nm)" package="5 mm [THT]"]
  元件6 = node32s

nets:
  N1: 元件1.IO25, 元件4.S
  N2: 元件1.IO14, DHT11_1.DATA
  VCC: 元件1.5V, OLED_I2C2.VDD, 元件4.NC, DHT11_1.VCC, J1.vcc, R3.Pin_1, R4.Pin_1, R6.Pin_1, R7.Pin_1, R9.Pin_1, R10.Pin_1, R12.Pin_1, R13.Pin_1, R15.Pin_1, R18.Pin_1
  GND: 元件1.GND, S1.Pin_3, S1.Pin_4, OLED_I2C2.GND, 元件4.GND, DHT11_1.GND, J1.gnd, 7_Segment1.common_anode, 7_Segment2.common_anode, 7_Segment3.common_anode, 7_Segment4.common_anode, S3.Pin_3, S3.Pin_4
  N3: 元件1.IO22, OLED_I2C2.SCK
  N4: 元件1.IO21, OLED_I2C2.SDA
  N5: 元件1.IO19, J1.pulse
  N6: 元件1.IO17, S1.Pin_1, S1.Pin_2
  N7: 元件1.IO16, S3.Pin_1, S3.Pin_2
  N8: 7_Segment1.Segment_E, R15.Pin_0
  N9: 7_Segment1.Segment_D, R18.Pin_0
  N10: 7_Segment1.Segment_A, R19.Pin_1
  N11: 7_Segment1.Segment_F, R17.Pin_1
  N12: 7_Segment1.Segment_G, R16.Pin_1
  N13: 7_Segment2.Segment_E, R10.Pin_0
  N14: 7_Segment2.Segment_D, R3.Pin_0
  N15: 7_Segment2.Segment_C, R9.Pin_0
  N16: 7_Segment2.Segment_B, R1.Pin_1
  N17: 7_Segment2.Segment_A, R2.Pin_1
  N18: 7_Segment2.Segment_F, R5.Pin_1
  N19: 7_Segment3.Segment_E, R4.Pin_0
  N20: 7_Segment3.Segment_D, R13.Pin_0
  N21: 7_Segment3.Segment_C, R12.Pin_0
  N22: 7_Segment3.Segment_B, R14.Pin_1
  N23: 7_Segment3.Segment_F, R11.Pin_1
  N24: 7_Segment4.Segment_E, R6.Pin_0
  N25: 7_Segment4.Segment_D, R7.Pin_0
  N26: 7_Segment4.Segment_F, R8.Pin_1
  3.3V: 元件5.3.3V, RY2.power, 元件6.3.3V
  N27: 元件5.CHIP_PU, 元件6.CHIP_PU
  N28: 元件5.IO36, 元件6.IO36
  N29: 元件5.IO39, 元件6.IO39
  N30: 元件5.IO34, 元件6.IO34
  N31: 元件5.IO35, 元件6.IO35
  N32: 元件5.IO32, 元件6.IO32
  N33: 元件5.IO33, 元件6.IO33
  N34: 元件5.IO25, 元件6.IO25
  N35: 元件5.IO26, 元件6.IO26
  N36: 元件5.IO27, LED5.anode, LED6.anode, LED7.anode, 元件6.IO27
  N37: 元件5.IO14, 元件6.IO14
  N38: 元件5.IO12, 元件6.IO12
  N39: 元件5.V_BATT, 元件6.V_BATT
  N40: 元件5.IO13, 元件6.IO13
  N41: 元件5.IO9, LED4.anode, 元件6.IO9
  N42: 元件5.IO10, 元件6.IO10
  N43: 元件5.IO11, 元件6.IO11
  5V: 元件5.5V, 元件6.5V
  GND_2: 元件5.GND, RY2.ground, R21.Pin_0, R22.Pin_0, R23.Pin_0, R24.Pin_0, R25.Pin_0, R26.Pin_0, R27.Pin_0, 元件6.GND
  N44: 元件5.IO23, 元件6.IO23
  N45: 元件5.IO22, 元件6.IO22
  N46: 元件5.TXD, 元件6.TXD
  N47: 元件5.RXD, 元件6.RXD
  N48: 元件5.IO21, 元件6.IO21
  N49: 元件5.IO19, 元件6.IO19
  N50: 元件5.IO18, 元件6.IO18
  N51: 元件5.IO5, 元件6.IO5
  N52: 元件5.IO17, LED2.anode, LED3.anode, LED1.anode, 元件6.IO17
  N53: 元件5.IO16, 元件6.IO16
  N54: 元件5.IO4, 元件6.IO4
  N55: 元件5.IO0, 元件6.IO0
  N56: 元件5.IO2, 元件6.IO2
  N57: 元件5.IO15, RY2.signal, 元件6.IO15
  N58: 元件5.IO8, 元件6.IO8
  N59: 元件5.IO7, 元件6.IO7
  N60: 元件5.IO6, 元件6.IO6
  N61: M2.pin_1, VCC2.-
  N62: M2.pin_2, RY2.NO
  N63: RY2.C, VCC2.+
  N64: R1.Pin_0, R2.Pin_0, R5.Pin_0, R8.Pin_0, R11.Pin_0, R14.Pin_0, R16.Pin_0, R17.Pin_0, R19.Pin_0
  N65: LED2.cathode, R27.Pin_1
  N66: LED3.cathode, R26.Pin_1
  N67: LED4.cathode, R21.Pin_1
  N68: LED5.cathode, R22.Pin_1
  N69: LED6.cathode, R24.Pin_1
  N70: LED7.cathode, R23.Pin_1
  N71: R25.Pin_1, LED1.cathode

notes:
  T3-GPIO15
  T9-GPIO32
  21(SDA)
  T4-GPIO13
  Touch_Draw
  25
  蜂鳴器
  19
  伺服馬達
  Touch_Match1
  Touch_Match2
  22(SCL)
  DHT11
  14
  OLED
  L
  按鈕_Match
  17
  按鈕_Draw
  16
  O
  V
  E
  繼電器
  15
  LED
  09
  27
  T0-GPIO04
  Touch_Snow

custom parts:
  DHT11 module: https://cdn-learn.adafruit.com/downloads/pdf/dht.pdf DHT11 black pcb module reference by:https://github.com/adafruit/Fritzing-Library/blob/master/parts/DHT11%20Humitidy%20and%20Temperature%20Sensor.fzpz
  KF-301 Relay: KF-301 SPDT Relay module using SRD-05VDC-SL-C relay.
